# Fritzing sketch Untitled Sketch (saved by Fritzing 0.9.6b)
circuit board: 8.46667cm x 5.64444cm
breadboards: 1

parts:
  LED1 = LED - 3mm [color="Green (565nm)" current=0.030 package="3 mm [THT]"]
  LED2 = LED - 3mm [color="Red (633nm)" current=0.030 package="3 mm [THT]"]
  R1 = Resistor [tolerance=±5% resistance=330 package="0402 [SMD]"]  # not connected
  R2 = Resistor [tolerance=±5% resistance=330 package="0402 [SMD]"]  # not connected
  Componente1 = Arduino Uno (Rev3)
  HC-SR04_Sensor_1 = HC-SR04 Ultrasonic Distance Sensor
  U1 = JOYSTICK-PSP1000 [package=joystick-psp1000]  # not connected

nets:
  N1: LED1.anode, Componente1.D3_PWM
  N2: LED2.anode, Componente1.D5_PWM
  N3: Componente1.D8, HC-SR04_Sensor_1.TRIG
  N4: Componente1.D7, HC-SR04_Sensor_1.ECHO
  5V: Componente1.5V, HC-SR04_Sensor_1.VCC
  GND: Componente1.GND, HC-SR04_Sensor_1.GND
